# Fritzing sketch speedfighter (saved by Fritzing 0.9.3b)
perfboards: 1

parts:
  Raspberry_Pi_2 = Raspberry Pi 3 [part_number=RPI-3-V1.2]
  S9 = Pushbutton [package="[SMD]"]
  S10 = Pushbutton [package="[SMD]"]
  S11 = Pushbutton [package="[SMD]"]
  LED4 = smd LED [color="Red (633nm)" package="0603 [SMD]"]
  Mod3 = KY-019 5V Relay Module [package="Breakout board"]  # not connected
  LED5 = smd LED [color="Red (633nm)" package="0603 [SMD]"]
  R11 = Resistor [tolerance=±5% resistance=330 package="0805 [SMD]"]
  R12 = Resistor [tolerance=±5% resistance=330 package="0805 [SMD]"]

nets:
  N1: Raspberry_Pi_2.GPIO4, R12.Pin_0
  N2: Raspberry_Pi_2.GPIO17, R11.Pin_0
  N3: Raspberry_Pi_2.GPIO27, S9.Pin_3, S9.Pin_4
  N4: Raspberry_Pi_2.GND, LED5.cathode
  N5: Raspberry_Pi_2.GPIO24, S11.Pin_3, S11.Pin_4
  N6: Raspberry_Pi_2.GPIO23, S10.Pin_3, S10.Pin_4
  N7: S9.Pin_1, S9.Pin_2
  N8: S10.Pin_1, S10.Pin_2
  N9: S11.Pin_1, S11.Pin_2
  N10: LED4.anode, R11.Pin_1
  N11: LED5.anode, R12.Pin_1

custom parts:
  KY-019 5V Relay Module: KY-019 5V Relay module, used to control AC circuits. (Special thanks to vanepp for fixing the PCB holes and other errors)
